# Fritzing sketch Breadboard Setup v2 (saved by Fritzing 0.9.0b)
breadboards: 1

parts:
  R1 = Resistor [tolerance=±5% resistance=220 package=THT]
  R2 = Resistor [tolerance=±5% resistance=220 package=THT]
  R3 = Resistor [tolerance=±5% resistance=220 package=THT]
  R4 = Resistor [tolerance=±5% resistance=220 package=THT]
  R5 = Resistor [tolerance=±5% resistance=220 package=THT]
  R6 = Resistor [tolerance=±5% resistance=220 package=THT]
  R7 = Resistor [tolerance=±5% resistance=1M package=THT]
  R8 = Resistor [tolerance=±5% resistance=1M package=THT]
  R9 = Resistor [tolerance=±5% resistance=1M package=THT]
  R10 = Resistor [tolerance=±5% resistance=1M package=THT]
  R11 = Resistor [tolerance=±5% resistance=1M package=THT]
  R12 = Resistor [tolerance=±5% resistance=1M package=THT]
  R13 = Resistor [tolerance=±5% resistance=1k package=THT]
  R14 = TRIMPOT [package=3386u]
  S1 = Toggle Switch [package=THT]
  R15 = Resistor [tolerance=±5% resistance=1k package=THT]
  P1 = S1133 Si Photodiode [package="8mm Ceramic [THT]"]
  P2 = S1133 Si Photodiode [package="8mm Ceramic [THT]"]
  P3 = S1133 Si Photodiode [package="8mm Ceramic [THT]"]
  P4 = S1133 Si Photodiode [package="8mm Ceramic [THT]"]
  P5 = S1133 Si Photodiode [package="8mm Ceramic [THT]"]
  P6 = S1133 Si Photodiode [package="8mm Ceramic [THT]"]
  Q1 = MOSFET-NCHANNEL [package=to-92]
  Q2 = MOSFET-NCHANNEL [package=to-92]
  Q3 = MOSFET-NCHANNEL [package=to-92]
  Q4 = MOSFET-NCHANNEL [package=to-92]
  Q5 = MOSFET-NCHANNEL [package=to-92]
  Q6 = MOSFET-NCHANNEL [package=to-92]
  IC2 = IC, DIP package, 16 pins [chip_label=74LS151N]
  5V = male pin header, 1 pin [form="♂ (male)"]
  B1 = male pin header, 1 pin [form="♂ (male)"]
  A2 = male pin header, 1 pin [form="♂ (male)"]
  E7 = male pin header, 1 pin [form="♂ (male)"]
  E9 = male pin header, 1 pin [form="♂ (male)"]
  E11 = male pin header, 1 pin [form="♂ (male)"]
  3V = male pin header, 1 pin [form="♂ (male)"]
  A1 = male pin header, 1 pin [form="♂ (male)"]
  GND = male pin header, 1 pin [form="♂ (male)"]
  LED2 = Red LED - 5mm [package="5 mm [THT]"]
  LED3 = Red LED - 5mm [package="5 mm [THT]"]
  LED4 = Red LED - 5mm [package="5 mm [THT]"]
  LED5 = Red LED - 5mm [package="5 mm [THT]"]
  LED6 = Red LED - 5mm [package="5 mm [THT]"]
  LED1 = Red LED - 5mm [package="5 mm [THT]"]

nets:
  N1: R1.Pin_0, Q1.S, IC2.pin4
  N2: R1.Pin_1, R2.Pin_1, R3.Pin_1, R4.Pin_1, R5.Pin_1, R6.Pin_1, R14.CW, S1.COM, S1.L2, P1.anode, P2.anode, P3.anode, P4.anode, P5.anode, P6.anode, IC2.pin7, IC2.pin8, GND.pin1, LED2.anode, LED3.anode, LED4.anode, LED5.anode, LED6.anode, LED1.anode
  N3: R2.Pin_0, Q2.S, IC2.pin3
  N4: R3.Pin_0, Q4.S, IC2.pin1
  N5: R4.Pin_0, Q3.S, IC2.pin2
  N6: R5.Pin_0, Q5.S, IC2.pin15
  N7: R6.Pin_0, Q6.S, IC2.pin14
  N8: R7.Pin_0, R8.Pin_0, R9.Pin_0, R10.Pin_0, R11.Pin_0, R12.Pin_0, Q1.D, Q2.D, Q3.D, Q4.D, Q5.D, Q6.D, IC2.pin16, 5V.pin1, LED2.cathode, LED3.cathode, LED4.cathode, LED5.cathode, LED6.cathode, LED1.cathode
  N9: R7.Pin_1, P1.cathode, Q1.G
  N10: R8.Pin_1, P2.cathode, Q2.G
  N11: R9.Pin_1, P3.cathode, Q3.G
  N12: R10.Pin_1, P4.cathode, Q4.G
  N13: R11.Pin_1, P5.cathode, Q5.G
  N14: R12.Pin_1, P6.cathode, Q6.G
  N15: R13.Pin_0, R15.Pin_0, 3V.pin1
  N16: R13.Pin_1, R14.CCW
  N17: R14.WIPER, A2.pin1
  N18: S1.L1, R15.Pin_1, B1.pin1
  N19: IC2.pin5, A1.pin1
  N20: IC2.pin9, E11.pin1
  N21: IC2.pin10, E9.pin1
  N22: IC2.pin11, E7.pin1

notes:
  6 x photodiodes
  6 x laser diodes
  GND
  5V
  3V
  A1
  Input Capture
  A2
  Volume
  B1
  Electric Mode
  E7 E9 E11
  MUX cycling pins

custom parts:
  TRIMPOT: Various small potentiometers for set-and-forget applications
  S1133 Si Photodiode: S1133 photodiode with low dark current by Hamamatsu.
  MOSFET-NCHANNEL: Generic NMOS footprint
  Red LED - 5mm: A generic red LED (~1.8V)
