# Fritzing sketch Breadboard Setup (saved by Fritzing 0.9.0b)
breadboards: 1

parts:
  P1 = S1133 Si Photodiode [package="8mm Ceramic [THT]"]
  R1 = Resistor [tolerance=±5% resistance=1M package=THT]
  R2 = TRIMPOT [package=3386u]
  R3 = Resistor [tolerance=±5% resistance=1k package=THT]
  S1 = Toggle Switch [package=THT]
  R4 = Resistor [tolerance=±5% resistance=10k package=THT]

nets:
  N1: P1.cathode, R1.Pin_1
  N2: P1.anode, R2.CW
  N3: R1.Pin_0, R3.Pin_0, R4.Pin_0
  N4: R2.CCW, R3.Pin_1
  N5: S1.L1, R4.Pin_1
  N6: S1.COM, S1.L2

notes:
  Volume control
  1k potentiometer
  B7
  A1
  B1
  3V
  GND

custom parts:
  TRIMPOT: Various small potentiometers for set-and-forget applications
