# Fritzing sketch Veroboard Setup (saved by Fritzing 0.9.0b)
stripboards: 1

parts:
  VCC1 = Battery block 9V
  IC1 = Voltage Regulator [package=78xxl]
  D1 = Rectifier Diode [part_number=1N4001 package="300 mil [THT]"]
  P2 = S1133 Si Photodiode [package="8mm Ceramic [THT]"]
  C1 = Electrolytic Capacitor [capacitance=1µF package="100 mil [THT, electrolytic]"]
  C2 = Electrolytic Capacitor [capacitance=1µF package="100 mil [THT, electrolytic]"]
  Q1 = MOSFET-NCHANNEL [package=to-92]
  R5 = Resistor [tolerance=±5% resistance=220 package=THT]
  LED3 = Red LED - 5mm [package="5 mm [THT]"]
  P3 = S1133 Si Photodiode [package="8mm Ceramic [THT]"]
  Q2 = MOSFET-NCHANNEL [package=to-92]
  R7 = Resistor [tolerance=±5% resistance=220 package=THT]
  LED4 = Red LED - 5mm [package="5 mm [THT]"]
  R8 = Resistor [tolerance=±5% resistance=1M package=THT]
  R9 = Resistor [tolerance=±5% resistance=1M package=THT]
  P4 = S1133 Si Photodiode [package="8mm Ceramic [THT]"]
  Q3 = MOSFET-NCHANNEL [package=to-92]
  R10 = Resistor [tolerance=±5% resistance=1M package=THT]
  Q4 = MOSFET-NCHANNEL [package=to-92]
  LED5 = Red LED - 5mm [package="5 mm [THT]"]
  P5 = S1133 Si Photodiode [package="8mm Ceramic [THT]"]
  R11 = Resistor [tolerance=±5% resistance=220 package=THT]
  LED6 = Red LED - 5mm [package="5 mm [THT]"]
  R12 = Resistor [tolerance=±5% resistance=1M package=THT]
  R13 = Resistor [tolerance=±5% resistance=220 package=THT]
  P6 = S1133 Si Photodiode [package="8mm Ceramic [THT]"]
  Q5 = MOSFET-NCHANNEL [package=to-92]
  R14 = Resistor [tolerance=±5% resistance=1M package=THT]
  Q6 = MOSFET-NCHANNEL [package=to-92]
  LED7 = Red LED - 5mm [package="5 mm [THT]"]
  P7 = S1133 Si Photodiode [package="8mm Ceramic [THT]"]
  R15 = Resistor [tolerance=±5% resistance=220 package=THT]
  LED8 = Red LED - 5mm [package="5 mm [THT]"]
  R16 = Resistor [tolerance=±5% resistance=1M package=THT]
  R17 = Resistor [tolerance=±5% resistance=220 package=THT]
  IC4 = IC, DIP package, 16 pins [chip_label=74LS151N]
  E7 = female pin header, 1 pin [form="♀ (female)"]
  GND = female pin header, 1 pin [form="♀ (female)"]
  E11 = female pin header, 1 pin [form="♀ (female)"]
  3V = female pin header, 1 pin [form="♀ (female)"]
  5V = female pin header, 1 pin [form="♀ (female)"]
  E9 = female pin header, 1 pin [form="♀ (female)"]
  A1 = female pin header, 1 pin [form="♀ (female)"]
  R18 = Rotary Potentiometer (Large) [maximum_resistance=268kΩ package=THT]
  R19 = Resistor [tolerance=±5% resistance=220k package=THT]
  A2 = female pin header, 1 pin [form="♀ (female)"]
  S1 = Toggle Switch [package=THT]
  R20 = Resistor [tolerance=±5% resistance=1k package=THT]
  B1 = female pin header, 1 pin [form="♀ (female)"]
  Q7 = NPN-Transistor [package="TO92 [THT]"]
  LED9 = LED - 5mm [color="Red (633nm)" package="5 mm [THT]"]
  R21 = Resistor [tolerance=±5% resistance=220 package=THT]
  Q8 = NPN-Transistor [package="TO92 [THT]"]
  R22 = Resistor [tolerance=±5% resistance=220 package=THT]
  LED10 = LED - 5mm [color="Red (633nm)" package="5 mm [THT]"]
  Q9 = NPN-Transistor [package="TO92 [THT]"]
  LED11 = LED - 5mm [color="Red (633nm)" package="5 mm [THT]"]
  LED12 = LED - 5mm [color="Red (633nm)" package="5 mm [THT]"]
  R23 = Resistor [tolerance=±5% resistance=220 package=THT]
  Q10 = NPN-Transistor [package="TO92 [THT]"]
  R25 = Resistor [tolerance=±5% resistance=220 package=THT]
  Q11 = NPN-Transistor [package="TO92 [THT]"]
  LED13 = LED - 5mm [color="Red (633nm)" package="5 mm [THT]"]
  R26 = Resistor [tolerance=±5% resistance=220 package=THT]
  Q12 = NPN-Transistor [package="TO92 [THT]"]
  LED14 = LED - 5mm [color="Red (633nm)" package="5 mm [THT]"]
  R28 = Resistor [tolerance=±5% resistance=220 package=THT]

nets:
  N1: VCC1.-, IC1.GND, D1.anode, P2.anode, C1.-, C2.-, R5.Pin_1, LED3.cathode, P3.anode, R7.Pin_1, LED4.cathode, P4.anode, LED5.cathode, P5.anode, R11.Pin_1, LED6.cathode, R13.Pin_1, P6.anode, LED7.cathode, P7.anode, R15.Pin_1, LED8.cathode, R17.Pin_1, IC4.pin7, IC4.pin8, GND.pin1, R18.leg2, S1.COM, S1.L2, R21.Pin_1, R22.Pin_1, R23.Pin_1, R25.Pin_1, R26.Pin_1, R28.Pin_1
  N2: VCC1.+, IC1.IN, D1.cathode, C1.+
  N3: IC1.OUT, C2.+, Q1.D, LED3.anode, Q2.D, LED4.anode, R8.Pin_1, R9.Pin_1, Q3.D, R10.Pin_1, Q4.D, LED5.anode, LED6.anode, R12.Pin_1, Q5.D, R14.Pin_1, Q6.D, LED7.anode, LED8.anode, R16.Pin_1, IC4.pin16, 5V.pin1, LED9.anode, LED10.anode, LED11.anode, LED12.anode, LED13.anode, LED14.anode
  N4: P2.cathode, Q1.G, R8.Pin_0
  N5: Q1.S, R5.Pin_0, IC4.pin14, Q7.B
  N6: P3.cathode, Q2.G, R9.Pin_0
  N7: Q2.S, R7.Pin_0, IC4.pin15, Q8.B
  N8: P4.cathode, Q4.G, R12.Pin_0
  N9: Q3.S, R11.Pin_0, IC4.pin2, Q10.B
  N10: Q3.G, R10.Pin_0, P5.cathode
  N11: Q4.S, R13.Pin_0, IC4.pin1, Q9.B
  N12: P6.cathode, Q6.G, R16.Pin_0
  N13: Q5.S, R15.Pin_0, IC4.pin4, Q12.B
  N14: Q5.G, R14.Pin_0, P7.cathode
  N15: Q6.S, R17.Pin_0, IC4.pin3, Q11.B
  N16: IC4.pin5, A1.pin1
  N17: IC4.pin9, E11.pin1
  N18: IC4.pin10, E9.pin1
  N19: IC4.pin11, E7.pin1
  N20: 3V.pin1, R19.Pin_1, R20.Pin_1
  N21: R18.leg1, R19.Pin_0
  N22: R18.wiper, A2.pin1
  N23: S1.L1, R20.Pin_0, B1.pin1
  N24: Q7.E, R21.Pin_0
  N25: Q7.C, LED9.cathode
  N26: Q8.E, R22.Pin_0
  N27: Q8.C, LED10.cathode
  N28: Q9.E, R23.Pin_0
  N29: Q9.C, LED11.cathode
  N30: LED12.cathode, Q10.C
  N31: Q10.E, R25.Pin_0
  N32: Q11.E, R28.Pin_0
  N33: Q11.C, LED13.cathode
  N34: R26.Pin_0, Q12.E
  N35: Q12.C, LED14.cathode

custom parts:
  S1133 Si Photodiode: S1133 photodiode with low dark current by Hamamatsu.
  MOSFET-NCHANNEL: Generic NMOS footprint
  Red LED - 5mm: A generic red LED (~1.8V)
