# Fritzing sketch fret-vb (saved by Fritzing 0.9.0b)
stripboards: 1

parts:
  S3 = Momentary Switch [package=ksa_sealed_tac_switch]
  S4 = Momentary Switch [package=ksa_sealed_tac_switch]
  S5 = Momentary Switch [package=ksa_sealed_tac_switch]
  R2 = Resistor [tolerance=±5% resistance=1k package=THT]
  R3 = Resistor [tolerance=±5% resistance=1.5k package=THT]
  R4 = Resistor [tolerance=±5% resistance=1.2k package=THT]
  R5 = Resistor [tolerance=±5% resistance=1.8k package=THT]
  R6 = Resistor [tolerance=±5% resistance=1k package=THT]
  J1 = female pin header, 1 pin [form="♀ (female)"]
  J2 = female pin header, 1 pin [form="♀ (female)"]
  S6 = Momentary Switch [package=ksa_sealed_tac_switch]
  S7 = Momentary Switch [package=ksa_sealed_tac_switch]
  S8 = Momentary Switch [package=ksa_sealed_tac_switch]
  S9 = Momentary Switch [package=ksa_sealed_tac_switch]
  S10 = Momentary Switch [package=ksa_sealed_tac_switch]
  R7 = Resistor [tolerance=±5% resistance=1k package=THT]
  R8 = Resistor [tolerance=±5% resistance=1.2k package=THT]
  R9 = Resistor [tolerance=±5% resistance=1.5k package=THT]
  R10 = Resistor [tolerance=±2% resistance=1.8k package=THT]
  R11 = Resistor [tolerance=±5% resistance=1k package=THT]
  J3 = female pin header, 1 pin [form="♀ (female)"]
  S11 = Momentary Switch [package=ksa_sealed_tac_switch]
  S12 = Momentary Switch [package=ksa_sealed_tac_switch]
  S13 = Momentary Switch [package=ksa_sealed_tac_switch]
  S14 = Momentary Switch [package=ksa_sealed_tac_switch]
  S15 = Momentary Switch [package=ksa_sealed_tac_switch]
  S16 = Momentary Switch [package=ksa_sealed_tac_switch]
  S17 = Momentary Switch [package=ksa_sealed_tac_switch]
  S18 = Momentary Switch [package=ksa_sealed_tac_switch]
  R12 = Resistor [tolerance=±5% resistance=1k package=THT]
  R13 = Resistor [tolerance=±5% resistance=1.2k package=THT]
  R14 = Resistor [tolerance=±5% resistance=1.2k package=THT]
  R15 = Resistor [tolerance=±5% resistance=1k package=THT]
  R16 = Resistor [tolerance=±5% resistance=1.5k package=THT]
  R17 = Resistor [tolerance=±5% resistance=1.8k package=THT]
  R18 = Resistor [tolerance=±5% resistance=1.5k package=THT]
  R19 = Resistor [tolerance=±5% resistance=1.8k package=THT]
  R20 = Resistor [tolerance=±5% resistance=1k package=THT]
  R21 = Resistor [tolerance=±5% resistance=1k package=THT]
  J4 = female pin header, 1 pin [form="♀ (female)"]
  J5 = female pin header, 1 pin [form="♀ (female)"]
  S19 = Momentary Switch [package=ksa_sealed_tac_switch]
  S20 = Momentary Switch [package=ksa_sealed_tac_switch]
  S21 = Momentary Switch [package=ksa_sealed_tac_switch]
  S22 = Momentary Switch [package=ksa_sealed_tac_switch]
  S23 = Momentary Switch [package=ksa_sealed_tac_switch]
  S24 = Momentary Switch [package=ksa_sealed_tac_switch]
  S25 = Momentary Switch [package=ksa_sealed_tac_switch]
  S26 = Momentary Switch [package=ksa_sealed_tac_switch]
  R22 = Resistor [tolerance=±5% resistance=1.2k package=THT]
  R23 = Resistor [tolerance=±5% resistance=1k package=THT]
  R24 = Resistor [tolerance=±5% resistance=1k package=THT]
  R25 = Resistor [tolerance=±5% resistance=1.2k package=THT]
  R26 = Resistor [tolerance=±5% resistance=1.8k package=THT]
  R27 = Resistor [tolerance=±5% resistance=1.5k package=THT]
  R28 = Resistor [tolerance=±5% resistance=1.5k package=THT]
  R29 = Resistor [tolerance=±5% resistance=1.8k package=THT]
  R30 = Resistor [tolerance=±5% resistance=1k package=THT]
  R31 = Resistor [tolerance=±5% resistance=1k package=THT]
  J6 = female pin header, 1 pin [form="♀ (female)"]
  J7 = female pin header, 1 pin [form="♀ (female)"]

nets:
  N1: S3.1, S4.1, S5.1, S6.1, S7.1, S8.1, S9.1, S10.1, S11.1, S12.1, S13.1, S14.1, S15.1, S16.1, S17.1, S18.1, S19.1, S20.1, S21.1, S22.1, S23.1, S24.1, S25.1, S26.1
  N2: S3.4, R4.Pin_1
  N3: S4.4, R3.Pin_1
  N4: S5.4, R5.Pin_1
  N5: R2.Pin_0, R3.Pin_0, R4.Pin_0, R5.Pin_0, R6.Pin_1, J2.pin1
  N6: R2.Pin_1, S6.4
  N7: R6.Pin_0, J1.pin1, R11.Pin_0, R20.Pin_0, R21.Pin_0, R30.Pin_0, R31.Pin_0
  N8: S7.4, R9.Pin_1
  N9: S8.4, R10.Pin_1
  N10: S9.4, R7.Pin_1
  N11: S10.4, R8.Pin_1
  N12: R7.Pin_0, R8.Pin_0, R9.Pin_0, R10.Pin_0, R11.Pin_1, J3.pin1
  N13: S11.4, R17.Pin_1
  N14: S12.4, R12.Pin_1
  N15: S13.4, R18.Pin_1
  N16: S14.4, R19.Pin_1
  N17: S15.4, R13.Pin_1
  N18: S16.4, R16.Pin_1
  N19: S17.4, R14.Pin_1
  N20: S18.4, R15.Pin_1
  N21: R12.Pin_0, R14.Pin_0, R17.Pin_0, R18.Pin_0, R21.Pin_1, J5.pin1
  N22: R13.Pin_0, R15.Pin_0, R16.Pin_0, R19.Pin_0, R20.Pin_1, J4.pin1
  N23: S19.4, R26.Pin_1
  N24: S20.4, R24.Pin_1
  N25: S21.4, R25.Pin_1
  N26: S22.4, R29.Pin_1
  N27: S23.4, R23.Pin_1
  N28: S24.4, R27.Pin_1
  N29: S25.4, R22.Pin_1
  N30: S26.4, R28.Pin_1
  N31: R22.Pin_0, R24.Pin_0, R26.Pin_0, R28.Pin_0, R30.Pin_1, J7.pin1
  N32: R23.Pin_0, R25.Pin_0, R27.Pin_0, R29.Pin_0, R31.Pin_1, J6.pin1
