# Fritzing sketch fret (saved by Fritzing 0.9.0b)
breadboards: 1

parts:
  S1 = Momentary Switch [package=ksa_sealed_tac_switch]
  S2 = Momentary Switch [package=ksa_sealed_tac_switch]
  S3 = Momentary Switch [package=ksa_sealed_tac_switch]
  S4 = Momentary Switch [package=ksa_sealed_tac_switch]
  R1 = Resistor [tolerance=±5% resistance=1k package=THT]
  R2 = Resistor [tolerance=±5% resistance=1.2k package=THT]
  R3 = Resistor [tolerance=±5% resistance=1.5k package=THT]
  R4 = Resistor [tolerance=±5% resistance=1.8k package=THT]
  R5 = Resistor [tolerance=±5% resistance=1k package=THT]
  J1 = female pin header, 1 pin [form="♀ (female)"]
  J2 = female pin header, 1 pin [form="♀ (female)"]

nets:
  N1: S1.2, S2.2, S3.2, S4.2
  N2: S1.3, R1.Pin_1
  N3: S2.3, R2.Pin_1
  N4: S3.3, R3.Pin_1
  N5: S4.3, R4.Pin_1
  N6: R1.Pin_0, R2.Pin_0, R3.Pin_0, R4.Pin_0, R5.Pin_0, J1.pin1
  N7: R5.Pin_1, J2.pin1
